// Logisim project finalProject.circ as structural Verilog
module main (
  input  in_1,
  input  in_2,
  input  in_3,
  input  f0,
  input  f1,
  input  f2,
  input  [7:0] in_7,
  input  [7:0] in_8,
  input  [7:0] in_9,
  input  [7:0] in_10,
  output [2:0] out_11,
  output out_12,
  output out_13,
  output out_14,
  output [7:0] out_15,
  output [7:0] out_16
);

  wire and_1_out, and_2_out, and_3_out, clock_1_out, comparator_1_verif, not_1_out, not_2_out, not_3_out,
       not_4_out, not_5_out, or_1_out, or_2_out;
  wire [1:0] codificator_1_outputpentruselectie;
  wire [7:0] muxmare_1_output, muxmic_1_iesire, registrupe8biti_1_data_out;

  Clock clock_1 (.out(clock_1_out));
  not not_1 (not_1_out, out_11[0]);
  not not_2 (not_2_out, out_11[1]);
  not not_3 (not_3_out, out_11[2]);
  or or_1 (or_1_out, f0, f1, f2);
  Codificator codificator_1 (.f0(f0), .f1(f1), .f2(f2), .outputPentruSelectie(codificator_1_outputpentruselectie));
  and and_1 (and_1_out, not_1_out, not_2_out, not_3_out);
  unitateControlCola unitatecontrolcola_1 (
    .clk(clock_1_out), .F3(in_1), .F4(in_2), .FS(in_3), .pesteLeu(comparator_1_verif), .punemCoin(or_1_out),
    .AM(out_12), .AT(out_13), .RM(out_14), .stareCurenta(out_11));
  not not_4 (not_4_out, out_11[1]);
  MuxMare muxmare_1 (
    .sel(codificator_1_outputpentruselectie), .input0(in_7), .input1(in_8), .input2(in_9), .input3(in_10),
    .\output (muxmare_1_output));
  and and_2 (and_2_out, out_11[2], not_4_out, out_11[0]);
  not not_5 (not_5_out, out_11[0]);
  and and_3 (and_3_out, out_11[2], out_11[1], not_5_out);
  sumator8bits sumator8bits_1 (.r(and_1_out), .a(muxmic_1_iesire), .b(muxmare_1_output), .sum(out_16));
  or or_2 (or_2_out, and_2_out, and_3_out);
  RegistruPe8Biti registrupe8biti_1 (
    .clk(clock_1_out), .reset(and_1_out), .data_in(out_16), .data_out(registrupe8biti_1_data_out));
  Comparator comparator_1 (.Numar(out_16), .verif(comparator_1_verif));
  Rest rest_1 (.suma(out_16), .en(or_2_out), .stare(out_11), .\final (out_15));
  MuxMic muxmic_1 (.w0(registrupe8biti_1_data_out), .w1(muxmic_1_iesire), .sel(or_1_out), .iesire(muxmic_1_iesire));
endmodule

// VHDL entity unitateControlCola, as the project stores it:
--------------------------------------------------------------------------------
-- Project :
-- File    :
-- Autor   :
-- Date    :
--
--------------------------------------------------------------------------------
-- Description :
--
--------------------------------------------------------------------------------

LIBRARY ieee;
USE ieee.std_logic_1164.all;

ENTITY unitateControlCola IS
  PORT (
  ------------------------------------------------------------------------------
  --Insert input ports below
    clk         	: IN  std_logic;                    -- input bit example
    F3		  	: IN std_logic;
    F4			: IN std_logic;
    FS			: IN std_logic;
    pesteLeu   	: in std_logic;
    punemCoin 		: in std_logic;
  ------------------------------------------------------------------------------
  --Insert output ports below
    AM		  	: out std_logic;
    AT			: out std_logic;
    RM			: out std_logic;                  -- output bit example
    stareCurenta	: OUT std_logic_vector(2 DOWNTO 0)  -- output vector example
    );
END unitateControlCola;

--------------------------------------------------------------------------------
--Complete your VHDL description below
--------------------------------------------------------------------------------

ARCHITECTURE unitateControlCola OF unitateControlCola IS

signal stareActuala : std_logic_vector(2 downto 0) := "000";
BEGIN

	process(clk)
		begin
		if(rising_edge(clk)) then
			if( stareActuala = "000") then
				if(FS = '1') then 
					stareActuala <= "000";
					AT <= '0';
					AM <= '0';
					RM <= '0';
				else
					stareActuala <= "001";
					AT <= '0';
					AM <= '0';
					RM <= '0';
				end if;
				
			elsif( stareActuala = "001" ) then
				if(punemCoin = '0') then
					stareActuala <= "010";
					AT <= '0';
					AM <= '0';
					RM <= '0';
				else
					AT <= '0';
					AM <= '1';
					RM <= '0';
					stareActuala <="010";
				end if;
			elsif( stareActuala = "010") then
				if( punemCoin = '0') then
					stareActuala <= "011";
					AT <= '0';
					AM <= '0';
					RM <= '0';
				else
					stareActuala <= "010";
					AT <= '0';
					AM <= '0';
					RM <= '0';
				end if;
			elsif( stareActuala = "011") then
				if(F4 = '1') then
					stareActuala <= "100";
					AT <= '0';
					AM <= '0';
					RM <= '0';
				else
					stareActuala <= "001";
					AT <= '0';
					AM <= '0';
					RM <= '0';
				end if;
			elsif( stareActuala ="100") then
				if(pesteLeu ='1') then
					stareActuala <= "101";
					AT <= '1';
					AM <= '0';
					RM <= '0';
				else
					stareActuala <= "110";
					AT <= '0';
					AM <= '0';
					RM <= '1';
				end if;
			elsif ( stareActuala = "101") then
					stareActuala <= "000";
					AT <= '1';
					AM <= '0';
					RM <= '0';	
			end if;
			elsif( stareActuala = "110") then
					stareActuala <= "000";
					AT <= '0';
					AM <= '0';
					RM <= '1';

					
		end if;			
		stareCurenta <= stareActuala;	

	

	end process;
END unitateControlCola;

// VHDL entity MuxMic, as the project stores it:
--------------------------------------------------------------------------------
-- Project :
-- File    :
-- Autor   :
-- Date    :
--
--------------------------------------------------------------------------------
-- Description :
--
--------------------------------------------------------------------------------

LIBRARY ieee;
USE ieee.std_logic_1164.all;

ENTITY MuxMic IS
  PORT (
  ------------------------------------------------------------------------------
  --Insert input ports below
    w0     	 : IN  std_logic_vector (7 downto 0);          
    w1        	 : IN  std_logic_vector (7 downto 0);   
    sel         : IN  std_logic;
  ------------------------------------------------------------------------------
  --Insert output ports below
    iesire        : out  std_logic_vector (7 downto 0)  
    
    );
END MuxMic;

--------------------------------------------------------------------------------
--Complete your VHDL description below
--------------------------------------------------------------------------------

ARCHITECTURE MuxMic OF MuxMic IS

BEGIN

	process(w0,w1,sel)
	begin
		if(sel ='0')then
			iesire <= w0;
		elsif (sel ='1') then
			iesire <=w1;
		else
			iesire <= x"00";
		end if;
	end process;

END MuxMic;

// VHDL entity MuxMare, as the project stores it:
--------------------------------------------------------------------------------
-- Project :
-- File    :
-- Autor   :
-- Date    :
--
--------------------------------------------------------------------------------
-- Description :
--
--------------------------------------------------------------------------------

LIBRARY ieee;
USE ieee.std_logic_1164.all;

ENTITY MuxMare IS
  PORT (
  ------------------------------------------------------------------------------
  --Insert input ports below
   	   sel    : in  STD_LOGIC_VECTOR(1 downto 0);
        input0 : in  STD_LOGIC_VECTOR(7 downto 0);
        input1 : in  STD_LOGIC_VECTOR(7 downto 0);
        input2 : in  STD_LOGIC_VECTOR(7 downto 0);
        input3 : in  STD_LOGIC_VECTOR(7 downto 0);
        
  ------------------------------------------------------------------------------
  --Insert output ports below
  
    output : out STD_LOGIC_VECTOR(7 downto 0)
    );
END MuxMare;

--------------------------------------------------------------------------------
--Complete your VHDL description below
--------------------------------------------------------------------------------

ARCHITECTURE TypeArchitecture OF MuxMare IS

BEGIN

 process(sel, input0, input1, input2, input3)
    begin
        case sel is
            when "00" =>
                output <= input0;
            when "01" =>
                output <= input1;
            when "10" =>
                output <= input2;
            when others =>
                output <= input3;
        end case;
    end process;


END TypeArchitecture;

// VHDL entity RegistruPe8Biti, as the project stores it:
--------------------------------------------------------------------------------
-- Project :
-- File    :
-- Autor   :
-- Date    :
--
--------------------------------------------------------------------------------
-- Description :
--
--------------------------------------------------------------------------------

LIBRARY ieee;
USE ieee.std_logic_1164.all;

ENTITY RegistruPe8Biti IS
  PORT (
  ------------------------------------------------------------------------------
  --Insert input ports below
    clk    : in  STD_LOGIC;
        reset  : in  STD_LOGIC;
        
        data_in: in  STD_LOGIC_VECTOR(7 downto 0);
  ------------------------------------------------------------------------------
  --Insert output ports below
   data_out: out STD_LOGIC_VECTOR(7 downto 0)
    );
END RegistruPe8Biti;

--------------------------------------------------------------------------------
--Complete your VHDL description below
--------------------------------------------------------------------------------

ARCHITECTURE TypeArchitecture OF RegistruPe8Biti IS

	 signal register_data : STD_LOGIC_VECTOR(7 downto 0) := (others => '0');
BEGIN

	process(clk, reset)
    begin
        if reset = '1' then
            register_data <= (others => '0');
        elsif rising_edge(clk) then
           
                register_data <= data_in;
            
        end if;
    end process;

    data_out <= register_data;

END TypeArchitecture;

// VHDL entity Codificator, as the project stores it:
--------------------------------------------------------------------------------
-- Project :
-- File    :
-- Autor   :
-- Date    :
--
--------------------------------------------------------------------------------
-- Description :
--
--------------------------------------------------------------------------------

LIBRARY ieee;
USE ieee.std_logic_1164.all;

ENTITY Codificator IS
  PORT (
  ------------------------------------------------------------------------------
  --Insert input ports below
    f0,f1,f2              : IN  std_logic;                    -- input bit example

  ------------------------------------------------------------------------------
  --Insert output ports below
    outputPentruSelectie    : OUT std_logic_vector(1 DOWNTO 0)  -- output vector example
    );
END Codificator;

--------------------------------------------------------------------------------
--Complete your VHDL description below
--------------------------------------------------------------------------------

ARCHITECTURE TypeArchitecture OF Codificator IS

BEGIN
        process(f0,f1,f2)
        variable inputBus : std_logic_vector(2 downto 0) := "000";
            begin
            inputBus := f0&f1&f2;
                if(inputBus = "100") then
                    outputPentruSelectie <= "01";
                elsif(inputBus = "010") then
                    outputPentruSelectie <= "10";
                elsif(inputBus = "001") then
                    outputPentruSelectie <= "11";
                else
                    outputPentruSelectie <= "00";
                end if;

        end process;

END TypeArchitecture;

// VHDL entity Comparator, as the project stores it:
--------------------------------------------------------------------------------
-- Project :
-- File    :
-- Autor   :
-- Date    :
--
--------------------------------------------------------------------------------
-- Description :
--
--------------------------------------------------------------------------------

LIBRARY ieee;
USE ieee.std_logic_1164.all;

use IEEE.STD_LOGIC_UNSIGNED.ALL;
ENTITY Comparator IS
  PORT (
  ------------------------------------------------------------------------------
  --Insert input ports below
  
       Numar : IN STD_LOGIC_VECTOR(7 DOWNTO 0);
  ------------------------------------------------------------------------------
  --Insert output ports below
  	verif : OUT STD_LOGIC
    );
END Comparator;

--------------------------------------------------------------------------------
--Complete your VHDL description below
--------------------------------------------------------------------------------

ARCHITECTURE TypeArchitecture OF Comparator IS

BEGIN
	process(Numar)
		begin
			IF("01100100">Numar)then
				verif <= '0';
			else
				verif <= '1';
			end if;
	end process;

END TypeArchitecture;

// VHDL entity sumator8bits, as the project stores it:
LIBRARY ieee;
USE ieee.std_logic_1164.all;
use IEEE.STD_LOGIC_UNSIGNED.ALL;
ENTITY sumator8bits IS
  PORT (
          r : in STD_LOgic;
         a, b: IN STD_LOGIC_VECTOR(7 DOWNTO 0);
        sum: OUT STD_LOGIC_VECTOR(7 DOWNTO 0)
    );
END sumator8bits;

--------------------------------------------------------------------------------
--Complete your VHDL description below
--------------------------------------------------------------------------------

ARCHITECTURE TypeArchitecture OF sumator8bits IS

BEGIN
    process(r,a,b)
    begin
        if(r='1')then
            sum <= x"00";
        else
              sum <= a + b;

        end if;
    end process;

END TypeArchitecture;

// VHDL entity Rest, as the project stores it:
LIBRARY ieee;
USE ieee.std_logic_1164.all;

use IEEE.STD_LOGIC_UNSIGNED.ALL;

ENTITY Rest IS
  PORT (
  ------------------------------------------------------------------------------
  --Insert input ports below
    suma       : IN  std_logic_vector(7 downto 0); -- suma pe 8 bits
    en         : IN  std_logic; -- input vector example
    stare      : in std_logic_vector(2 downto 0);
  ------------------------------------------------------------------------------

    final  : OUT std_logic_vector(7 DOWNTO 0)  -- output vector example
    );
END Rest;

--------------------------------------------------------------------------------
--Complete your VHDL description below
--------------------------------------------------------------------------------

ARCHITECTURE TypeArchitecture OF Rest IS
BEGIN

    process(en, stare, suma)
        begin 
            if(en = '1') then
                if(stare = "101")    then
                    final <= suma - "01100100";
                elsif(stare = "110") then
                    final <= suma;
                else
                    final <= x"00";
                end if;
            else
                final <= x"00";
            end if;
    end process;

END TypeArchitecture;
